# Fritzing sketch board (saved by Fritzing 0.9.3b)
breadboards: 2

parts:
  S1 = Pushbutton [package=THT]
  R1 = Resistor [tolerance=±5% resistance=10k package=THT]
  R2 = Resistor [tolerance=±5% resistance=10k package=THT]
  RHT1 = Humidity and Temperature Sensor RHT03
  J1 = male pin header, 2 pins [form="♂ (male)"]
  C1 = Electrolytic Capacitor [capacitance=10µF voltage=50V package="100 mil [THT, electrolytic]"]
  C2 = Tantalum Capacitor [capacitance=100nF voltage=50V package="100 mil [THT, tantalum]"]
  U5 = Voltage Regulator - 3.3V [package="TO220 [THT]"]
  R3 = Resistor [tolerance=±5% resistance=10k package=THT]
  U6 = ESP8266-07 [part_number=ESP8266]

nets:
  N1: S1.leg0, RHT1.GND_2, R3.Pin_0, U6.GND
  N2: S1.leg1, U6.GPIO_0
  N3: R1.Pin_0, U6.REST
  VCC: R1.Pin_1, R2.Pin_1, RHT1.Vcc, U6.VCC
  N4: R2.Pin_0, U6.CH_PD
  N5: RHT1.Data-signal, R3.Pin_1, U6.GPIO_5
  N6: J1.pin1, U6.RXD
  N7: J1.pin2, U6.TXD
  N8: C1.-, U5.input_voltage
  N9: C2.+, U5.output_voltage

custom parts:
  ESP8266-07: ESP8266 - 07 WiFi Module on PCB
